// Logisim project ExpMatrixcontroller.circ as structural Verilog: 7 circuits, main circuit main
module main (
  input  in_out_prime,
  input  [7:0] I_Oaddr,
  input  I_Osel,
  input  [15:0] I_Odat,
  input  clock,
  output [15:0] I_Odat_2,
  output [31:0] out_7,
  output [31:0] out_8,
  output [31:0] out_9,
  output [31:0] out_10,
  output [31:0] out_11,
  output [31:0] out_12,
  output [31:0] out_13,
  output [31:0] out_14,
  output [31:0] out_15,
  output [31:0] out_16,
  output [31:0] out_17,
  output [31:0] out_18,
  output [31:0] out_19,
  output [31:0] out_20,
  output [31:0] out_21,
  output [31:0] out_22,
  output [31:0] out_23,
  output [31:0] out_24,
  output [31:0] out_25,
  output [31:0] out_26,
  output [31:0] out_27,
  output [31:0] out_28,
  output [31:0] out_29,
  output [31:0] out_30,
  output [31:0] out_31,
  output [31:0] out_32,
  output [31:0] out_33,
  output [31:0] out_34,
  output [31:0] out_35,
  output [31:0] out_36,
  output [31:0] out_37,
  output [31:0] out_38
);

  wire and_1_out, and_2_out, and_3_out, and_4_out, and_5_out, and_6_out, and_7_out, and_8_out, and_9_out,
       and_10_out, and_11_out, gameprocessor_1_cc;
  wire [15:0] buffer_1_narrowout, controlled_buffer_1_out, controlled_buffer_3_out, controlled_buffer_5_out,
       Status1_q, Status2_q;
  wire [31:0] wi0, wi1, wi2, wi3, wi4, wi5, wi6, wi7, wi8, wi9, wi10, wi11, wi12, wi13, wi14, wi15, wi16,
       wi17, wi18, wi19, wi20, wi21, wi22, wi23, wi24, wi25, wi26, wi27, wi28, wi29, wi30, wi31;

  and and_1 (and_1_out, I_Osel, I_Oaddr[7]);
  and and_2 (and_2_out, ~in_out_prime, and_1_out);  // AND_Gate
  assign controlled_buffer_1_out = and_2_out ? I_Odat : 16'bz;  // Controlled_Buffer controlled_buffer_1
  assign I_Odat_2 = and_3_out ? buffer_1_narrowout : 16'bz;  // Controlled_Buffer controlled_buffer_2
  and and_3 (and_3_out, in_out_prime, and_1_out);
  buffer buffer_1 (
    .sel(and_1_out), .addr(I_Oaddr[6:1]), .narrowin(controlled_buffer_1_out), .rd_wr_prime(in_out_prime),
    .reset(controlled_buffer_5_out[10]), .clock(clock), .in_9(wi0), .in_10(wi1), .in_11(wi2), .in_12(wi3),
    .in_13(wi4), .in_14(wi5), .in_15(wi6), .in_16(wi7), .in_17(wi8), .in_18(wi9), .in_19(wi10), .in_20(wi11),
    .in_21(wi12), .in_22(wi13), .in_23(wi14), .in_24(wi15), .in_25(wi16), .in_26(wi17), .in_27(wi18),
    .in_28(wi19), .in_29(wi20), .in_30(wi21), .in_31(wi22), .in_32(wi23), .in_33(wi24), .in_34(wi25),
    .in_35(wi26), .in_36(wi27), .in_37(wi28), .in_38(wi29), .in_39(wi30), .in_40(wi31),
    .narrowout(buffer_1_narrowout), .out_42(out_7), .out_43(out_8), .out_44(out_9), .out_45(out_10),
    .out_46(out_11), .out_47(out_12), .out_48(out_13), .out_49(out_14), .out_50(out_15), .out_51(out_16),
    .out_52(out_17), .out_53(out_18), .out_54(out_19), .out_55(out_20), .out_56(out_21), .out_57(out_22),
    .out_58(out_23), .out_59(out_24), .out_60(out_25), .out_61(out_26), .out_62(out_27), .out_63(out_28),
    .out_64(out_29), .out_65(out_30), .out_66(out_31), .out_67(out_32), .out_68(out_33), .out_69(out_34),
    .out_70(out_35), .out_71(out_36), .out_72(out_37), .out_73(out_38), .play(Status2_q[9]),
    .cc(gameprocessor_1_cc));
  gameProcessor gameprocessor_1 (
    .cc(gameprocessor_1_cc), .clock(clock), .play(Status2_q[9]), .surv(Status1_q[8:0]),
    .born(Status2_q[8:0]), .in_5(out_7), .in_6(out_8), .in_7(out_9), .in_8(out_10), .in_9(out_11),
    .in_10(out_12), .in_11(out_13), .in_12(out_14), .in_13(out_15), .in_14(out_16), .in_15(out_17),
    .in_16(out_18), .in_17(out_19), .in_18(out_20), .in_19(out_21), .in_20(out_22), .in_21(out_23),
    .in_22(out_24), .in_23(out_25), .in_24(out_26), .in_25(out_27), .in_26(out_28), .in_27(out_29),
    .in_28(out_30), .in_29(out_31), .in_30(out_32), .in_31(out_33), .in_32(out_34), .in_33(out_35),
    .in_34(out_36), .in_35(out_37), .in_36(out_38), .out_38(wi0), .out_39(wi1), .out_40(wi2), .out_41(wi3),
    .out_42(wi4), .out_43(wi5), .out_44(wi6), .out_45(wi7), .out_46(wi8), .out_47(wi9), .out_48(wi10),
    .out_49(wi11), .out_50(wi12), .out_51(wi13), .out_52(wi14), .out_53(wi15), .out_54(wi16), .out_55(wi17),
    .out_56(wi18), .out_57(wi19), .out_58(wi20), .out_59(wi21), .out_60(wi22), .out_61(wi23), .out_62(wi24),
    .out_63(wi25), .out_64(wi26), .out_65(wi27), .out_66(wi28), .out_67(wi29), .out_68(wi30), .out_69(wi31));
  and and_4 (and_4_out, ~I_Oaddr[7], I_Oaddr[6], I_Oaddr[5], I_Oaddr[4], I_Oaddr[3], I_Oaddr[2], I_Oaddr[1], ~I_Oaddr[0]);  // AND_Gate
  and and_5 (and_5_out, I_Osel, and_4_out);
  and and_6 (and_6_out, ~in_out_prime, and_5_out);  // AND_Gate
  assign controlled_buffer_3_out = and_6_out ? I_Odat : 16'bz;  // Controlled_Buffer controlled_buffer_3
  assign I_Odat_2 = and_7_out ? Status1_q : 16'bz;  // Controlled_Buffer controlled_buffer_4
  and and_7 (and_7_out, in_out_prime, and_5_out);
  Register #(.width(16)) Status1 (
    .D(controlled_buffer_3_out), .en(and_5_out), .Q(Status1_q), .clk(clock));  // open: clr
  and and_8 (and_8_out, ~I_Oaddr[7], I_Oaddr[6], I_Oaddr[5], I_Oaddr[4], I_Oaddr[3], I_Oaddr[2], ~I_Oaddr[1], ~I_Oaddr[0]);  // AND_Gate
  and and_9 (and_9_out, I_Osel, and_8_out);
  and and_10 (and_10_out, ~in_out_prime, and_9_out);  // AND_Gate
  assign controlled_buffer_5_out = and_10_out ? I_Odat : 16'bz;  // Controlled_Buffer controlled_buffer_5
  Pull_Resistor pull_resistor_1 (.node(controlled_buffer_5_out[10]));
  assign I_Odat_2 = and_11_out ? Status2_q : 16'bz;  // Controlled_Buffer controlled_buffer_6
  and and_11 (and_11_out, in_out_prime, and_9_out);
  Register #(.width(16)) Status2 (
    .D(controlled_buffer_5_out), .en(and_9_out), .Q(Status2_q), .clk(clock));  // open: clr

  // Other names for the same wires on the sheet: wo0[31:0] = out_7; wo1[31:0] = out_8; wo2[31:0] = out_9;
  //   wo3[31:0] = out_10; wo4[31:0] = out_11; wo5[31:0] = out_12; wo6[31:0] = out_13; wo7[31:0] = out_14;
  //   wo8[31:0] = out_15; wo9[31:0] = out_16; wo10[31:0] = out_17; wo11[31:0] = out_18; wo12[31:0] = out_19;
  //   wo13[31:0] = out_20; wo14[31:0] = out_21; wo15[31:0] = out_22; wo16[31:0] = out_23; wo17[31:0] = out_24;
  //   wo18[31:0] = out_25; wo19[31:0] = out_26; wo20[31:0] = out_27; wo21[31:0] = out_28; wo22[31:0] = out_29;
  //   wo23[31:0] = out_30; wo24[31:0] = out_31; wo25[31:0] = out_32; wo26[31:0] = out_33; wo27[31:0] = out_34;
  //   wo28[31:0] = out_35; wo29[31:0] = out_36; wo30[31:0] = out_37; wo31[31:0] = out_38
endmodule

module buffer (
  input  clock,
  input  sel,
  input  [5:0] addr,
  input  cc,
  input  [15:0] narrowin,
  input  rd_wr_prime,
  input  reset,
  input  play,
  input  [31:0] in_9,
  input  [31:0] in_10,
  input  [31:0] in_11,
  input  [31:0] in_12,
  input  [31:0] in_13,
  input  [31:0] in_14,
  input  [31:0] in_15,
  input  [31:0] in_16,
  input  [31:0] in_17,
  input  [31:0] in_18,
  input  [31:0] in_19,
  input  [31:0] in_20,
  input  [31:0] in_21,
  input  [31:0] in_22,
  input  [31:0] in_23,
  input  [31:0] in_24,
  input  [31:0] in_25,
  input  [31:0] in_26,
  input  [31:0] in_27,
  input  [31:0] in_28,
  input  [31:0] in_29,
  input  [31:0] in_30,
  input  [31:0] in_31,
  input  [31:0] in_32,
  input  [31:0] in_33,
  input  [31:0] in_34,
  input  [31:0] in_35,
  input  [31:0] in_36,
  input  [31:0] in_37,
  input  [31:0] in_38,
  input  [31:0] in_39,
  input  [31:0] in_40,
  output [15:0] narrowout,
  output [31:0] out_42,
  output [31:0] out_43,
  output [31:0] out_44,
  output [31:0] out_45,
  output [31:0] out_46,
  output [31:0] out_47,
  output [31:0] out_48,
  output [31:0] out_49,
  output [31:0] out_50,
  output [31:0] out_51,
  output [31:0] out_52,
  output [31:0] out_53,
  output [31:0] out_54,
  output [31:0] out_55,
  output [31:0] out_56,
  output [31:0] out_57,
  output [31:0] out_58,
  output [31:0] out_59,
  output [31:0] out_60,
  output [31:0] out_61,
  output [31:0] out_62,
  output [31:0] out_63,
  output [31:0] out_64,
  output [31:0] out_65,
  output [31:0] out_66,
  output [31:0] out_67,
  output [31:0] out_68,
  output [31:0] out_69,
  output [31:0] out_70,
  output [31:0] out_71,
  output [31:0] out_72,
  output [31:0] out_73
);

  wire bufferrow_2_block_2, bufferrow_2_countclock_2, bufferrow_2_play_2, bufferrow_2_rd_wr_prime_2,
       bufferrow_2_reset_2, bufferrow_3_block_2, bufferrow_3_countclock_2, bufferrow_3_play_2,
       bufferrow_3_rd_wr_prime_2, bufferrow_3_reset_2, bufferrow_4_block_2, bufferrow_4_countclock_2,
       bufferrow_4_play_2, bufferrow_4_rd_wr_prime_2, bufferrow_4_reset_2, bufferrow_5_block_2,
       bufferrow_5_countclock_2, bufferrow_5_play_2, bufferrow_5_rd_wr_prime_2, bufferrow_5_reset_2,
       bufferrow_6_block_2, bufferrow_6_countclock_2, bufferrow_6_play_2, bufferrow_6_rd_wr_prime_2,
       bufferrow_6_reset_2, bufferrow_7_block_2, bufferrow_7_countclock_2, bufferrow_7_play_2,
       bufferrow_7_rd_wr_prime_2, bufferrow_7_reset_2, bufferrow_8_block_2, bufferrow_8_countclock_2,
       bufferrow_8_play_2, bufferrow_8_rd_wr_prime_2, bufferrow_8_reset_2, bufferrow_9_block_2,
       bufferrow_9_countclock_2, bufferrow_9_play_2, bufferrow_9_rd_wr_prime_2, bufferrow_9_reset_2,
       bufferrow_10_block_2, bufferrow_10_countclock_2, bufferrow_10_play_2, bufferrow_10_rd_wr_prime_2,
       bufferrow_10_reset_2, bufferrow_11_block_2, bufferrow_11_countclock_2, bufferrow_11_play_2,
       bufferrow_11_rd_wr_prime_2, bufferrow_11_reset_2, bufferrow_12_block_2, bufferrow_12_countclock_2,
       bufferrow_12_play_2, bufferrow_12_rd_wr_prime_2, bufferrow_12_reset_2, bufferrow_13_block_2,
       bufferrow_13_countclock_2, bufferrow_13_play_2, bufferrow_13_rd_wr_prime_2, bufferrow_13_reset_2,
       bufferrow_14_block_2, bufferrow_14_countclock_2, bufferrow_14_play_2, bufferrow_14_rd_wr_prime_2,
       bufferrow_14_reset_2, bufferrow_15_block_2, bufferrow_15_countclock_2, bufferrow_15_play_2,
       bufferrow_15_rd_wr_prime_2, bufferrow_15_reset_2, bufferrow_16_block_2, bufferrow_16_countclock_2,
       bufferrow_16_play_2, bufferrow_16_rd_wr_prime_2, bufferrow_16_reset_2, bufferrow_17_block_2,
       bufferrow_17_countclock_2, bufferrow_17_play_2, bufferrow_17_rd_wr_prime_2, bufferrow_17_reset_2,
       bufferrow_18_block_2, bufferrow_18_countclock_2, bufferrow_18_play_2, bufferrow_18_rd_wr_prime_2,
       bufferrow_18_reset_2, bufferrow_19_block_2, bufferrow_19_countclock_2, bufferrow_19_play_2,
       bufferrow_19_rd_wr_prime_2, bufferrow_19_reset_2, bufferrow_20_block_2, bufferrow_20_countclock_2,
       bufferrow_20_play_2, bufferrow_20_rd_wr_prime_2, bufferrow_20_reset_2, bufferrow_21_block_2,
       bufferrow_21_countclock_2, bufferrow_21_play_2, bufferrow_21_rd_wr_prime_2, bufferrow_21_reset_2,
       bufferrow_22_block_2, bufferrow_22_countclock_2, bufferrow_22_play_2, bufferrow_22_rd_wr_prime_2,
       bufferrow_22_reset_2, bufferrow_23_block_2, bufferrow_23_countclock_2, bufferrow_23_play_2,
       bufferrow_23_rd_wr_prime_2, bufferrow_23_reset_2, bufferrow_24_block_2, bufferrow_24_countclock_2,
       bufferrow_24_play_2, bufferrow_24_rd_wr_prime_2, bufferrow_24_reset_2, bufferrow_25_block_2,
       bufferrow_25_countclock_2, bufferrow_25_play_2, bufferrow_25_rd_wr_prime_2, bufferrow_25_reset_2,
       bufferrow_26_block_2, bufferrow_26_countclock_2, bufferrow_26_play_2, bufferrow_26_rd_wr_prime_2,
       bufferrow_26_reset_2, bufferrow_27_block_2, bufferrow_27_countclock_2, bufferrow_27_play_2,
       bufferrow_27_rd_wr_prime_2, bufferrow_27_reset_2, bufferrow_28_block_2, bufferrow_28_countclock_2,
       bufferrow_28_play_2, bufferrow_28_rd_wr_prime_2, bufferrow_28_reset_2, bufferrow_29_block_2,
       bufferrow_29_countclock_2, bufferrow_29_play_2, bufferrow_29_rd_wr_prime_2, bufferrow_29_reset_2,
       bufferrow_30_block_2, bufferrow_30_countclock_2, bufferrow_30_play_2, bufferrow_30_rd_wr_prime_2,
       bufferrow_30_reset_2, bufferrow_31_block_2, bufferrow_31_countclock_2, bufferrow_31_play_2,
       bufferrow_31_rd_wr_prime_2, bufferrow_31_reset_2, bufferrow_32_block_2, bufferrow_32_countclock_2,
       bufferrow_32_play_2, bufferrow_32_rd_wr_prime_2, bufferrow_32_reset_2;
  wire [31:0] decoder_1_out0, demultiplexer_1_out0;

  Decoder #(.select(5), .disabled(0)) decoder_1 (
    .out0(decoder_1_out0[0]), .out1(decoder_1_out0[1]), .out2(decoder_1_out0[2]), .out3(decoder_1_out0[3]),
    .out4(decoder_1_out0[4]), .out5(decoder_1_out0[5]), .out6(decoder_1_out0[6]), .out7(decoder_1_out0[7]),
    .out8(decoder_1_out0[8]), .out9(decoder_1_out0[9]), .out10(decoder_1_out0[10]),
    .out11(decoder_1_out0[11]), .out12(decoder_1_out0[12]), .out13(decoder_1_out0[13]),
    .out14(decoder_1_out0[14]), .out15(decoder_1_out0[15]), .out16(decoder_1_out0[16]),
    .out17(decoder_1_out0[17]), .out18(decoder_1_out0[18]), .out19(decoder_1_out0[19]),
    .out20(decoder_1_out0[20]), .out21(decoder_1_out0[21]), .out22(decoder_1_out0[22]),
    .out23(decoder_1_out0[23]), .out24(decoder_1_out0[24]), .out25(decoder_1_out0[25]),
    .out26(decoder_1_out0[26]), .out27(decoder_1_out0[27]), .out28(decoder_1_out0[28]),
    .out29(decoder_1_out0[29]), .out30(decoder_1_out0[30]), .out31(decoder_1_out0[31]), .sel(addr[5:1]),
    .en(sel));
  bufferrow bufferrow_1 (
    .widein(in_9), .narrowin(narrowin), .rd_wr_prime(bufferrow_2_rd_wr_prime_2), .sel(decoder_1_out0[0]),
    .block(bufferrow_2_block_2), .reset(bufferrow_2_reset_2), .clock(demultiplexer_1_out0[0]),
    .narrowout(narrowout), .wideout(out_42), .countclock(bufferrow_2_countclock_2), .play(bufferrow_2_play_2));  // open: block_2, rd_wr_prime_2, reset_2, countclock_2, play_2
  bufferrow bufferrow_2 (
    .widein(in_10), .narrowin(narrowin), .rd_wr_prime(bufferrow_3_rd_wr_prime_2), .sel(decoder_1_out0[1]),
    .block(bufferrow_3_block_2), .reset(bufferrow_3_reset_2), .clock(demultiplexer_1_out0[1]),
    .narrowout(narrowout), .wideout(out_43), .block_2(bufferrow_2_block_2),
    .rd_wr_prime_2(bufferrow_2_rd_wr_prime_2), .reset_2(bufferrow_2_reset_2),
    .countclock(bufferrow_3_countclock_2), .countclock_2(bufferrow_2_countclock_2),
    .play(bufferrow_3_play_2), .play_2(bufferrow_2_play_2));
  bufferrow bufferrow_3 (
    .widein(in_11), .narrowin(narrowin), .rd_wr_prime(bufferrow_4_rd_wr_prime_2), .sel(decoder_1_out0[2]),
    .block(bufferrow_4_block_2), .reset(bufferrow_4_reset_2), .clock(demultiplexer_1_out0[2]),
    .narrowout(narrowout), .wideout(out_44), .block_2(bufferrow_3_block_2),
    .rd_wr_prime_2(bufferrow_3_rd_wr_prime_2), .reset_2(bufferrow_3_reset_2),
    .countclock(bufferrow_4_countclock_2), .countclock_2(bufferrow_3_countclock_2),
    .play(bufferrow_4_play_2), .play_2(bufferrow_3_play_2));
  bufferrow bufferrow_4 (
    .widein(in_12), .narrowin(narrowin), .rd_wr_prime(bufferrow_5_rd_wr_prime_2), .sel(decoder_1_out0[3]),
    .block(bufferrow_5_block_2), .reset(bufferrow_5_reset_2), .clock(demultiplexer_1_out0[3]),
    .narrowout(narrowout), .wideout(out_45), .block_2(bufferrow_4_block_2),
    .rd_wr_prime_2(bufferrow_4_rd_wr_prime_2), .reset_2(bufferrow_4_reset_2),
    .countclock(bufferrow_5_countclock_2), .countclock_2(bufferrow_4_countclock_2),
    .play(bufferrow_5_play_2), .play_2(bufferrow_4_play_2));
  bufferrow bufferrow_5 (
    .widein(in_13), .narrowin(narrowin), .rd_wr_prime(bufferrow_6_rd_wr_prime_2), .sel(decoder_1_out0[4]),
    .block(bufferrow_6_block_2), .reset(bufferrow_6_reset_2), .clock(demultiplexer_1_out0[4]),
    .narrowout(narrowout), .wideout(out_46), .block_2(bufferrow_5_block_2),
    .rd_wr_prime_2(bufferrow_5_rd_wr_prime_2), .reset_2(bufferrow_5_reset_2),
    .countclock(bufferrow_6_countclock_2), .countclock_2(bufferrow_5_countclock_2),
    .play(bufferrow_6_play_2), .play_2(bufferrow_5_play_2));
  bufferrow bufferrow_6 (
    .widein(in_14), .narrowin(narrowin), .rd_wr_prime(bufferrow_7_rd_wr_prime_2), .sel(decoder_1_out0[5]),
    .block(bufferrow_7_block_2), .reset(bufferrow_7_reset_2), .clock(demultiplexer_1_out0[5]),
    .narrowout(narrowout), .wideout(out_47), .block_2(bufferrow_6_block_2),
    .rd_wr_prime_2(bufferrow_6_rd_wr_prime_2), .reset_2(bufferrow_6_reset_2),
    .countclock(bufferrow_7_countclock_2), .countclock_2(bufferrow_6_countclock_2),
    .play(bufferrow_7_play_2), .play_2(bufferrow_6_play_2));
  bufferrow bufferrow_7 (
    .widein(in_15), .narrowin(narrowin), .rd_wr_prime(bufferrow_8_rd_wr_prime_2), .sel(decoder_1_out0[6]),
    .block(bufferrow_8_block_2), .reset(bufferrow_8_reset_2), .clock(demultiplexer_1_out0[6]),
    .narrowout(narrowout), .wideout(out_48), .block_2(bufferrow_7_block_2),
    .rd_wr_prime_2(bufferrow_7_rd_wr_prime_2), .reset_2(bufferrow_7_reset_2),
    .countclock(bufferrow_8_countclock_2), .countclock_2(bufferrow_7_countclock_2),
    .play(bufferrow_8_play_2), .play_2(bufferrow_7_play_2));
  bufferrow bufferrow_8 (
    .widein(in_16), .narrowin(narrowin), .rd_wr_prime(bufferrow_9_rd_wr_prime_2), .sel(decoder_1_out0[7]),
    .block(bufferrow_9_block_2), .reset(bufferrow_9_reset_2), .clock(demultiplexer_1_out0[7]),
    .narrowout(narrowout), .wideout(out_49), .block_2(bufferrow_8_block_2),
    .rd_wr_prime_2(bufferrow_8_rd_wr_prime_2), .reset_2(bufferrow_8_reset_2),
    .countclock(bufferrow_9_countclock_2), .countclock_2(bufferrow_8_countclock_2),
    .play(bufferrow_9_play_2), .play_2(bufferrow_8_play_2));
  bufferrow bufferrow_9 (
    .widein(in_17), .narrowin(narrowin), .rd_wr_prime(bufferrow_10_rd_wr_prime_2), .sel(decoder_1_out0[8]),
    .block(bufferrow_10_block_2), .reset(bufferrow_10_reset_2), .clock(demultiplexer_1_out0[8]),
    .narrowout(narrowout), .wideout(out_50), .block_2(bufferrow_9_block_2),
    .rd_wr_prime_2(bufferrow_9_rd_wr_prime_2), .reset_2(bufferrow_9_reset_2),
    .countclock(bufferrow_10_countclock_2), .countclock_2(bufferrow_9_countclock_2),
    .play(bufferrow_10_play_2), .play_2(bufferrow_9_play_2));
  bufferrow bufferrow_10 (
    .widein(in_18), .narrowin(narrowin), .rd_wr_prime(bufferrow_11_rd_wr_prime_2), .sel(decoder_1_out0[9]),
    .block(bufferrow_11_block_2), .reset(bufferrow_11_reset_2), .clock(demultiplexer_1_out0[9]),
    .narrowout(narrowout), .wideout(out_51), .block_2(bufferrow_10_block_2),
    .rd_wr_prime_2(bufferrow_10_rd_wr_prime_2), .reset_2(bufferrow_10_reset_2),
    .countclock(bufferrow_11_countclock_2), .countclock_2(bufferrow_10_countclock_2),
    .play(bufferrow_11_play_2), .play_2(bufferrow_10_play_2));
  bufferrow bufferrow_11 (
    .widein(in_19), .narrowin(narrowin), .rd_wr_prime(bufferrow_12_rd_wr_prime_2), .sel(decoder_1_out0[10]),
    .block(bufferrow_12_block_2), .reset(bufferrow_12_reset_2), .clock(demultiplexer_1_out0[10]),
    .narrowout(narrowout), .wideout(out_52), .block_2(bufferrow_11_block_2),
    .rd_wr_prime_2(bufferrow_11_rd_wr_prime_2), .reset_2(bufferrow_11_reset_2),
    .countclock(bufferrow_12_countclock_2), .countclock_2(bufferrow_11_countclock_2),
    .play(bufferrow_12_play_2), .play_2(bufferrow_11_play_2));
  bufferrow bufferrow_12 (
    .widein(in_20), .narrowin(narrowin), .rd_wr_prime(bufferrow_13_rd_wr_prime_2), .sel(decoder_1_out0[11]),
    .block(bufferrow_13_block_2), .reset(bufferrow_13_reset_2), .clock(demultiplexer_1_out0[11]),
    .narrowout(narrowout), .wideout(out_53), .block_2(bufferrow_12_block_2),
    .rd_wr_prime_2(bufferrow_12_rd_wr_prime_2), .reset_2(bufferrow_12_reset_2),
    .countclock(bufferrow_13_countclock_2), .countclock_2(bufferrow_12_countclock_2),
    .play(bufferrow_13_play_2), .play_2(bufferrow_12_play_2));
  bufferrow bufferrow_13 (
    .widein(in_21), .narrowin(narrowin), .rd_wr_prime(bufferrow_14_rd_wr_prime_2), .sel(decoder_1_out0[12]),
    .block(bufferrow_14_block_2), .reset(bufferrow_14_reset_2), .clock(demultiplexer_1_out0[12]),
    .narrowout(narrowout), .wideout(out_54), .block_2(bufferrow_13_block_2),
    .rd_wr_prime_2(bufferrow_13_rd_wr_prime_2), .reset_2(bufferrow_13_reset_2),
    .countclock(bufferrow_14_countclock_2), .countclock_2(bufferrow_13_countclock_2),
    .play(bufferrow_14_play_2), .play_2(bufferrow_13_play_2));
  bufferrow bufferrow_14 (
    .widein(in_22), .narrowin(narrowin), .rd_wr_prime(bufferrow_15_rd_wr_prime_2), .sel(decoder_1_out0[13]),
    .block(bufferrow_15_block_2), .reset(bufferrow_15_reset_2), .clock(demultiplexer_1_out0[13]),
    .narrowout(narrowout), .wideout(out_55), .block_2(bufferrow_14_block_2),
    .rd_wr_prime_2(bufferrow_14_rd_wr_prime_2), .reset_2(bufferrow_14_reset_2),
    .countclock(bufferrow_15_countclock_2), .countclock_2(bufferrow_14_countclock_2),
    .play(bufferrow_15_play_2), .play_2(bufferrow_14_play_2));
  bufferrow bufferrow_15 (
    .widein(in_23), .narrowin(narrowin), .rd_wr_prime(bufferrow_16_rd_wr_prime_2), .sel(decoder_1_out0[14]),
    .block(bufferrow_16_block_2), .reset(bufferrow_16_reset_2), .clock(demultiplexer_1_out0[14]),
    .narrowout(narrowout), .wideout(out_56), .block_2(bufferrow_15_block_2),
    .rd_wr_prime_2(bufferrow_15_rd_wr_prime_2), .reset_2(bufferrow_15_reset_2),
    .countclock(bufferrow_16_countclock_2), .countclock_2(bufferrow_15_countclock_2),
    .play(bufferrow_16_play_2), .play_2(bufferrow_15_play_2));
  bufferrow bufferrow_16 (
    .widein(in_24), .narrowin(narrowin), .rd_wr_prime(bufferrow_17_rd_wr_prime_2), .sel(decoder_1_out0[15]),
    .block(bufferrow_17_block_2), .reset(bufferrow_17_reset_2), .clock(demultiplexer_1_out0[15]),
    .narrowout(narrowout), .wideout(out_57), .block_2(bufferrow_16_block_2),
    .rd_wr_prime_2(bufferrow_16_rd_wr_prime_2), .reset_2(bufferrow_16_reset_2),
    .countclock(bufferrow_17_countclock_2), .countclock_2(bufferrow_16_countclock_2),
    .play(bufferrow_17_play_2), .play_2(bufferrow_16_play_2));
  bufferrow bufferrow_17 (
    .widein(in_25), .narrowin(narrowin), .rd_wr_prime(bufferrow_18_rd_wr_prime_2), .sel(decoder_1_out0[16]),
    .block(bufferrow_18_block_2), .reset(bufferrow_18_reset_2), .clock(demultiplexer_1_out0[16]),
    .narrowout(narrowout), .wideout(out_58), .block_2(bufferrow_17_block_2),
    .rd_wr_prime_2(bufferrow_17_rd_wr_prime_2), .reset_2(bufferrow_17_reset_2),
    .countclock(bufferrow_18_countclock_2), .countclock_2(bufferrow_17_countclock_2),
    .play(bufferrow_18_play_2), .play_2(bufferrow_17_play_2));
  bufferrow bufferrow_18 (
    .widein(in_26), .narrowin(narrowin), .rd_wr_prime(bufferrow_19_rd_wr_prime_2), .sel(decoder_1_out0[17]),
    .block(bufferrow_19_block_2), .reset(bufferrow_19_reset_2), .clock(demultiplexer_1_out0[17]),
    .narrowout(narrowout), .wideout(out_59), .block_2(bufferrow_18_block_2),
    .rd_wr_prime_2(bufferrow_18_rd_wr_prime_2), .reset_2(bufferrow_18_reset_2),
    .countclock(bufferrow_19_countclock_2), .countclock_2(bufferrow_18_countclock_2),
    .play(bufferrow_19_play_2), .play_2(bufferrow_18_play_2));
  bufferrow bufferrow_19 (
    .widein(in_27), .narrowin(narrowin), .rd_wr_prime(bufferrow_20_rd_wr_prime_2), .sel(decoder_1_out0[18]),
    .block(bufferrow_20_block_2), .reset(bufferrow_20_reset_2), .clock(demultiplexer_1_out0[18]),
    .narrowout(narrowout), .wideout(out_60), .block_2(bufferrow_19_block_2),
    .rd_wr_prime_2(bufferrow_19_rd_wr_prime_2), .reset_2(bufferrow_19_reset_2),
    .countclock(bufferrow_20_countclock_2), .countclock_2(bufferrow_19_countclock_2),
    .play(bufferrow_20_play_2), .play_2(bufferrow_19_play_2));
  bufferrow bufferrow_20 (
    .widein(in_28), .narrowin(narrowin), .rd_wr_prime(bufferrow_21_rd_wr_prime_2), .sel(decoder_1_out0[19]),
    .block(bufferrow_21_block_2), .reset(bufferrow_21_reset_2), .clock(demultiplexer_1_out0[19]),
    .narrowout(narrowout), .wideout(out_61), .block_2(bufferrow_20_block_2),
    .rd_wr_prime_2(bufferrow_20_rd_wr_prime_2), .reset_2(bufferrow_20_reset_2),
    .countclock(bufferrow_21_countclock_2), .countclock_2(bufferrow_20_countclock_2),
    .play(bufferrow_21_play_2), .play_2(bufferrow_20_play_2));
  bufferrow bufferrow_21 (
    .widein(in_29), .narrowin(narrowin), .rd_wr_prime(bufferrow_22_rd_wr_prime_2), .sel(decoder_1_out0[20]),
    .block(bufferrow_22_block_2), .reset(bufferrow_22_reset_2), .clock(demultiplexer_1_out0[20]),
    .narrowout(narrowout), .wideout(out_62), .block_2(bufferrow_21_block_2),
    .rd_wr_prime_2(bufferrow_21_rd_wr_prime_2), .reset_2(bufferrow_21_reset_2),
    .countclock(bufferrow_22_countclock_2), .countclock_2(bufferrow_21_countclock_2),
    .play(bufferrow_22_play_2), .play_2(bufferrow_21_play_2));
  bufferrow bufferrow_22 (
    .widein(in_30), .narrowin(narrowin), .rd_wr_prime(bufferrow_23_rd_wr_prime_2), .sel(decoder_1_out0[21]),
    .block(bufferrow_23_block_2), .reset(bufferrow_23_reset_2), .clock(demultiplexer_1_out0[21]),
    .narrowout(narrowout), .wideout(out_63), .block_2(bufferrow_22_block_2),
    .rd_wr_prime_2(bufferrow_22_rd_wr_prime_2), .reset_2(bufferrow_22_reset_2),
    .countclock(bufferrow_23_countclock_2), .countclock_2(bufferrow_22_countclock_2),
    .play(bufferrow_23_play_2), .play_2(bufferrow_22_play_2));
  bufferrow bufferrow_23 (
    .widein(in_31), .narrowin(narrowin), .rd_wr_prime(bufferrow_24_rd_wr_prime_2), .sel(decoder_1_out0[22]),
    .block(bufferrow_24_block_2), .reset(bufferrow_24_reset_2), .clock(demultiplexer_1_out0[22]),
    .narrowout(narrowout), .wideout(out_64), .block_2(bufferrow_23_block_2),
    .rd_wr_prime_2(bufferrow_23_rd_wr_prime_2), .reset_2(bufferrow_23_reset_2),
    .countclock(bufferrow_24_countclock_2), .countclock_2(bufferrow_23_countclock_2),
    .play(bufferrow_24_play_2), .play_2(bufferrow_23_play_2));
  bufferrow bufferrow_24 (
    .widein(in_32), .narrowin(narrowin), .rd_wr_prime(bufferrow_25_rd_wr_prime_2), .sel(decoder_1_out0[23]),
    .block(bufferrow_25_block_2), .reset(bufferrow_25_reset_2), .clock(demultiplexer_1_out0[23]),
    .narrowout(narrowout), .wideout(out_65), .block_2(bufferrow_24_block_2),
    .rd_wr_prime_2(bufferrow_24_rd_wr_prime_2), .reset_2(bufferrow_24_reset_2),
    .countclock(bufferrow_25_countclock_2), .countclock_2(bufferrow_24_countclock_2),
    .play(bufferrow_25_play_2), .play_2(bufferrow_24_play_2));
  bufferrow bufferrow_25 (
    .widein(in_33), .narrowin(narrowin), .rd_wr_prime(bufferrow_26_rd_wr_prime_2), .sel(decoder_1_out0[24]),
    .block(bufferrow_26_block_2), .reset(bufferrow_26_reset_2), .clock(demultiplexer_1_out0[24]),
    .narrowout(narrowout), .wideout(out_66), .block_2(bufferrow_25_block_2),
    .rd_wr_prime_2(bufferrow_25_rd_wr_prime_2), .reset_2(bufferrow_25_reset_2),
    .countclock(bufferrow_26_countclock_2), .countclock_2(bufferrow_25_countclock_2),
    .play(bufferrow_26_play_2), .play_2(bufferrow_25_play_2));
  bufferrow bufferrow_26 (
    .widein(in_34), .narrowin(narrowin), .rd_wr_prime(bufferrow_27_rd_wr_prime_2), .sel(decoder_1_out0[25]),
    .block(bufferrow_27_block_2), .reset(bufferrow_27_reset_2), .clock(demultiplexer_1_out0[25]),
    .narrowout(narrowout), .wideout(out_67), .block_2(bufferrow_26_block_2),
    .rd_wr_prime_2(bufferrow_26_rd_wr_prime_2), .reset_2(bufferrow_26_reset_2),
    .countclock(bufferrow_27_countclock_2), .countclock_2(bufferrow_26_countclock_2),
    .play(bufferrow_27_play_2), .play_2(bufferrow_26_play_2));
  bufferrow bufferrow_27 (
    .widein(in_35), .narrowin(narrowin), .rd_wr_prime(bufferrow_28_rd_wr_prime_2), .sel(decoder_1_out0[26]),
    .block(bufferrow_28_block_2), .reset(bufferrow_28_reset_2), .clock(demultiplexer_1_out0[26]),
    .narrowout(narrowout), .wideout(out_68), .block_2(bufferrow_27_block_2),
    .rd_wr_prime_2(bufferrow_27_rd_wr_prime_2), .reset_2(bufferrow_27_reset_2),
    .countclock(bufferrow_28_countclock_2), .countclock_2(bufferrow_27_countclock_2),
    .play(bufferrow_28_play_2), .play_2(bufferrow_27_play_2));
  bufferrow bufferrow_28 (
    .widein(in_36), .narrowin(narrowin), .rd_wr_prime(bufferrow_29_rd_wr_prime_2), .sel(decoder_1_out0[27]),
    .block(bufferrow_29_block_2), .reset(bufferrow_29_reset_2), .clock(demultiplexer_1_out0[27]),
    .narrowout(narrowout), .wideout(out_69), .block_2(bufferrow_28_block_2),
    .rd_wr_prime_2(bufferrow_28_rd_wr_prime_2), .reset_2(bufferrow_28_reset_2),
    .countclock(bufferrow_29_countclock_2), .countclock_2(bufferrow_28_countclock_2),
    .play(bufferrow_29_play_2), .play_2(bufferrow_28_play_2));
  bufferrow bufferrow_29 (
    .widein(in_37), .narrowin(narrowin), .rd_wr_prime(bufferrow_30_rd_wr_prime_2), .sel(decoder_1_out0[28]),
    .block(bufferrow_30_block_2), .reset(bufferrow_30_reset_2), .clock(demultiplexer_1_out0[28]),
    .narrowout(narrowout), .wideout(out_70), .block_2(bufferrow_29_block_2),
    .rd_wr_prime_2(bufferrow_29_rd_wr_prime_2), .reset_2(bufferrow_29_reset_2),
    .countclock(bufferrow_30_countclock_2), .countclock_2(bufferrow_29_countclock_2),
    .play(bufferrow_30_play_2), .play_2(bufferrow_29_play_2));
  bufferrow bufferrow_30 (
    .widein(in_38), .narrowin(narrowin), .rd_wr_prime(bufferrow_31_rd_wr_prime_2), .sel(decoder_1_out0[29]),
    .block(bufferrow_31_block_2), .reset(bufferrow_31_reset_2), .clock(demultiplexer_1_out0[29]),
    .narrowout(narrowout), .wideout(out_71), .block_2(bufferrow_30_block_2),
    .rd_wr_prime_2(bufferrow_30_rd_wr_prime_2), .reset_2(bufferrow_30_reset_2),
    .countclock(bufferrow_31_countclock_2), .countclock_2(bufferrow_30_countclock_2),
    .play(bufferrow_31_play_2), .play_2(bufferrow_30_play_2));
  bufferrow bufferrow_31 (
    .widein(in_39), .narrowin(narrowin), .rd_wr_prime(bufferrow_32_rd_wr_prime_2), .sel(decoder_1_out0[30]),
    .block(bufferrow_32_block_2), .reset(bufferrow_32_reset_2), .clock(demultiplexer_1_out0[30]),
    .narrowout(narrowout), .wideout(out_72), .block_2(bufferrow_31_block_2),
    .rd_wr_prime_2(bufferrow_31_rd_wr_prime_2), .reset_2(bufferrow_31_reset_2),
    .countclock(bufferrow_32_countclock_2), .countclock_2(bufferrow_31_countclock_2),
    .play(bufferrow_32_play_2), .play_2(bufferrow_31_play_2));
  bufferrow bufferrow_32 (
    .widein(in_40), .narrowin(narrowin), .rd_wr_prime(rd_wr_prime), .sel(decoder_1_out0[31]),
    .block(addr[0]), .reset(reset), .clock(demultiplexer_1_out0[31]), .narrowout(narrowout),
    .wideout(out_73), .block_2(bufferrow_32_block_2), .rd_wr_prime_2(bufferrow_32_rd_wr_prime_2),
    .reset_2(bufferrow_32_reset_2), .countclock(cc), .countclock_2(bufferrow_32_countclock_2), .play(play),
    .play_2(bufferrow_32_play_2));
  Demultiplexer #(.select(5), .disabled(0)) demultiplexer_1 (
    .out0(demultiplexer_1_out0[0]), .out1(demultiplexer_1_out0[1]), .out2(demultiplexer_1_out0[2]),
    .out3(demultiplexer_1_out0[3]), .out4(demultiplexer_1_out0[4]), .out5(demultiplexer_1_out0[5]),
    .out6(demultiplexer_1_out0[6]), .out7(demultiplexer_1_out0[7]), .out8(demultiplexer_1_out0[8]),
    .out9(demultiplexer_1_out0[9]), .out10(demultiplexer_1_out0[10]), .out11(demultiplexer_1_out0[11]),
    .out12(demultiplexer_1_out0[12]), .out13(demultiplexer_1_out0[13]), .out14(demultiplexer_1_out0[14]),
    .out15(demultiplexer_1_out0[15]), .out16(demultiplexer_1_out0[16]), .out17(demultiplexer_1_out0[17]),
    .out18(demultiplexer_1_out0[18]), .out19(demultiplexer_1_out0[19]), .out20(demultiplexer_1_out0[20]),
    .out21(demultiplexer_1_out0[21]), .out22(demultiplexer_1_out0[22]), .out23(demultiplexer_1_out0[23]),
    .out24(demultiplexer_1_out0[24]), .out25(demultiplexer_1_out0[25]), .out26(demultiplexer_1_out0[26]),
    .out27(demultiplexer_1_out0[27]), .out28(demultiplexer_1_out0[28]), .out29(demultiplexer_1_out0[29]),
    .out30(demultiplexer_1_out0[30]), .out31(demultiplexer_1_out0[31]), .in(clock), .sel(addr[5:1]), .en(sel));

  // Other names for the same wires on the sheet: addr_t[4:0] = addr[5:1]; wi0[31:0] = in_9; wi1[31:0] = in_10;
  //   wi2[31:0] = in_11; wi3[31:0] = in_12; wi4[31:0] = in_13; wi5[31:0] = in_14; wi6[31:0] = in_15;
  //   wi7[31:0] = in_16; wi8[31:0] = in_17; wi9[31:0] = in_18; wi10[31:0] = in_19; wi11[31:0] = in_20;
  //   wi12[31:0] = in_21; wi13[31:0] = in_22; wi14[31:0] = in_23; wi15[31:0] = in_24; wi16[31:0] = in_25;
  //   wi17[31:0] = in_26; wi18[31:0] = in_27; wi19[31:0] = in_28; wi20[31:0] = in_29; wi21[31:0] = in_30;
  //   wi22[31:0] = in_31; wi23[31:0] = in_32; wi24[31:0] = in_33; wi25[31:0] = in_34; wi26[31:0] = in_35;
  //   wi27[31:0] = in_36; wi28[31:0] = in_37; wi29[31:0] = in_38; wi30[31:0] = in_39; wi31[31:0] = in_40;
  //   wo0[31:0] = out_42; wo1[31:0] = out_43; wo2[31:0] = out_44; wo3[31:0] = out_45; wo4[31:0] = out_46;
  //   wo5[31:0] = out_47; wo6[31:0] = out_48; wo7[31:0] = out_49; wo8[31:0] = out_50; wo9[31:0] = out_51;
  //   wo10[31:0] = out_52; wo11[31:0] = out_53; wo12[31:0] = out_54; wo13[31:0] = out_55; wo14[31:0] = out_56;
  //   wo15[31:0] = out_57; wo16[31:0] = out_58; wo17[31:0] = out_59; wo18[31:0] = out_60; wo19[31:0] = out_61;
  //   wo20[31:0] = out_62; wo21[31:0] = out_63; wo22[31:0] = out_64; wo23[31:0] = out_65; wo24[31:0] = out_66;
  //   wo25[31:0] = out_67; wo26[31:0] = out_68; wo27[31:0] = out_69; wo28[31:0] = out_70; wo29[31:0] = out_71;
  //   wo30[31:0] = out_72; wo31[31:0] = out_73
endmodule

module bufferrow (
  input  [31:0] widein,
  input  reset,
  input  [15:0] narrowin,
  input  clock,
  input  sel,
  input  rd_wr_prime,
  input  block,
  input  countclock,
  input  play,
  output [31:0] wideout,
  output reset_2,
  output [15:0] narrowout,
  output rd_wr_prime_2,
  output block_2,
  output countclock_2,
  output play_2
);

  wire and_7_out, and_8_out, or_3_out, or_4_out;
  wire [15:0] and_2_out, and_3_out, and_4_out, and_5_out, or_2_out, or_5_out;
  wire [15:15] and_1_out, and_6_out, or_1_out, or_6_out;
  wire [31:0] multiplexer_1_out;

  and and_1 (and_1_out[15], sel, ~block);  // AND_Gate
  or or_1 (or_1_out[15], ~sel, block, rd_wr_prime);  // OR_Gate
  assign or_2_out = and_2_out | and_3_out;  // OR_Gate or_2, 16 bits wide
  assign and_2_out = {16{and_1_out[15]}} & narrowin;  // AND_Gate and_2, 16 bits wide
  assign and_3_out = {16{or_1_out[15]}} & wideout[31:16];  // AND_Gate and_3, 16 bits wide
  or or_3 (or_3_out, countclock, clock);
  or or_4 (or_4_out, sel, play);
  Multiplexer #(.width(32), .enable("false")) multiplexer_1 (
    .in0(widein), .in1({or_2_out, or_5_out}), .out(multiplexer_1_out), .sel(sel));
  assign or_5_out = and_5_out | and_4_out;  // OR_Gate or_5, 16 bits wide
  Register #(.width(32)) register_1 (.D(multiplexer_1_out), .en(or_4_out), .Q(wideout), .clk(or_3_out), .clr(reset));
  assign and_4_out = {16{and_6_out[15]}} & narrowin;  // AND_Gate and_4, 16 bits wide
  assign and_5_out = wideout[15:0] & {16{or_6_out[15]}};  // AND_Gate and_5, 16 bits wide
  and and_6 (and_6_out[15], sel, block);
  or or_6 (or_6_out[15], ~sel, ~block, rd_wr_prime);  // OR_Gate
  and and_7 (and_7_out, rd_wr_prime, sel, ~block);  // AND_Gate
  assign narrowout = and_7_out ? wideout[31:16] : 16'bz;  // Controlled_Buffer controlled_buffer_1
  and and_8 (and_8_out, rd_wr_prime, sel, block);
  assign narrowout = and_8_out ? wideout[15:0] : 16'bz;  // Controlled_Buffer controlled_buffer_2

  assign block_2 = block;
  assign countclock_2 = countclock;
  assign play_2 = play;
  assign rd_wr_prime_2 = rd_wr_prime;
  assign reset_2 = reset;

  // Other names for the same wires on the sheet: self[31:0] = wideout; cc = countclock
endmodule

module gameProcessorrow (
  input  [31:0] above,
  input  [8:0] surv,
  input  [8:0] born,
  input  [31:0] in_4,
  input  [31:0] bottom,
  output [31:0] out_6
);

  wire cell_1_out_14, cell_2_out_13, cell_2_out_14, cell_3_out_13, cell_3_out_14, cell_4_out_13,
       cell_4_out_14, cell_5_out_13, cell_5_out_14, cell_6_out_13, cell_6_out_14, cell_7_out_13,
       cell_7_out_14, cell_8_out_13, cell_8_out_14, cell_9_out_13, cell_9_out_14, cell_10_out_13,
       cell_10_out_14, cell_11_out_13, cell_11_out_14, cell_12_out_13, cell_12_out_14, cell_13_out_13,
       cell_13_out_14, cell_14_out_13, cell_14_out_14, cell_15_out_13, cell_15_out_14, cell_16_out_13,
       cell_16_out_14, cell_17_out_13, cell_17_out_14, cell_18_out_13, cell_18_out_14, cell_19_out_13,
       cell_19_out_14, cell_20_out_13, cell_20_out_14, cell_21_out_13, cell_21_out_14, cell_22_out_13,
       cell_22_out_14, cell_23_out_13, cell_23_out_14, cell_24_out_13, cell_24_out_14, cell_25_out_13,
       cell_25_out_14, cell_26_out_13, cell_26_out_14, cell_27_out_13, cell_27_out_14, cell_28_out_13,
       cell_28_out_14, cell_29_out_13, cell_29_out_14, cell_30_out_13, cell_30_out_14, cell_31_out_13,
       cell_31_out_14, cell_32_out_13;
  wire [8:0] cell_1_born_2, cell_1_surv_2, cell_2_born_2, cell_2_surv_2, cell_3_born_2, cell_3_surv_2,
       cell_4_born_2, cell_4_surv_2, cell_5_born_2, cell_5_surv_2, cell_6_born_2, cell_6_surv_2,
       cell_7_born_2, cell_7_surv_2, cell_8_born_2, cell_8_surv_2, cell_9_born_2, cell_9_surv_2,
       cell_10_born_2, cell_10_surv_2, cell_11_born_2, cell_11_surv_2, cell_12_born_2, cell_12_surv_2,
       cell_13_born_2, cell_13_surv_2, cell_14_born_2, cell_14_surv_2, cell_15_born_2, cell_15_surv_2,
       cell_16_born_2, cell_16_surv_2, cell_17_born_2, cell_17_surv_2, cell_18_born_2, cell_18_surv_2,
       cell_19_born_2, cell_19_surv_2, cell_20_born_2, cell_20_surv_2, cell_21_born_2, cell_21_surv_2,
       cell_22_born_2, cell_22_surv_2, cell_23_born_2, cell_23_surv_2, cell_24_born_2, cell_24_surv_2,
       cell_25_born_2, cell_25_surv_2, cell_26_born_2, cell_26_surv_2, cell_27_born_2, cell_27_surv_2,
       cell_28_born_2, cell_28_surv_2, cell_29_born_2, cell_29_surv_2, cell_30_born_2, cell_30_surv_2,
       cell_31_born_2, cell_31_surv_2;

  \cell  cell_1 (
    .surv(surv), .in_2(1'b0), .in_3(cell_2_out_13), .in_4(1'b0), .in_5(bottom[1]), .in_6(in_4[0]),
    .in_7(above[1]), .in_8(bottom[0]), .in_9(above[0]), .in_10(1'b0), .born(born), .out_14(cell_1_out_14),
    .born_2(cell_1_born_2), .surv_2(cell_1_surv_2), .out_15(out_6[0]));  // open: out_13
  \cell  cell_2 (
    .surv(cell_1_surv_2), .in_2(cell_1_out_14), .in_3(cell_3_out_13), .in_4(bottom[0]), .in_5(bottom[2]),
    .in_6(in_4[1]), .in_7(above[2]), .in_8(bottom[1]), .in_9(above[1]), .in_10(above[0]),
    .born(cell_1_born_2), .out_13(cell_2_out_13), .out_14(cell_2_out_14), .born_2(cell_2_born_2),
    .surv_2(cell_2_surv_2), .out_15(out_6[1]));
  \cell  cell_3 (
    .surv(cell_2_surv_2), .in_2(cell_2_out_14), .in_3(cell_4_out_13), .in_4(bottom[1]), .in_5(bottom[3]),
    .in_6(in_4[2]), .in_7(above[3]), .in_8(bottom[2]), .in_9(above[2]), .in_10(above[1]),
    .born(cell_2_born_2), .out_13(cell_3_out_13), .out_14(cell_3_out_14), .born_2(cell_3_born_2),
    .surv_2(cell_3_surv_2), .out_15(out_6[2]));
  \cell  cell_4 (
    .surv(cell_3_surv_2), .in_2(cell_3_out_14), .in_3(cell_5_out_13), .in_4(bottom[2]), .in_5(bottom[4]),
    .in_6(in_4[3]), .in_7(above[4]), .in_8(bottom[3]), .in_9(above[3]), .in_10(above[2]),
    .born(cell_3_born_2), .out_13(cell_4_out_13), .out_14(cell_4_out_14), .born_2(cell_4_born_2),
    .surv_2(cell_4_surv_2), .out_15(out_6[3]));
  \cell  cell_5 (
    .surv(cell_4_surv_2), .in_2(cell_4_out_14), .in_3(cell_6_out_13), .in_4(bottom[3]), .in_5(bottom[5]),
    .in_6(in_4[4]), .in_7(above[5]), .in_8(bottom[4]), .in_9(above[4]), .in_10(above[3]),
    .born(cell_4_born_2), .out_13(cell_5_out_13), .out_14(cell_5_out_14), .born_2(cell_5_born_2),
    .surv_2(cell_5_surv_2), .out_15(out_6[4]));
  \cell  cell_6 (
    .surv(cell_5_surv_2), .in_2(cell_5_out_14), .in_3(cell_7_out_13), .in_4(bottom[4]), .in_5(bottom[6]),
    .in_6(in_4[5]), .in_7(above[6]), .in_8(bottom[5]), .in_9(above[5]), .in_10(above[4]),
    .born(cell_5_born_2), .out_13(cell_6_out_13), .out_14(cell_6_out_14), .born_2(cell_6_born_2),
    .surv_2(cell_6_surv_2), .out_15(out_6[5]));
  \cell  cell_7 (
    .surv(cell_6_surv_2), .in_2(cell_6_out_14), .in_3(cell_8_out_13), .in_4(bottom[5]), .in_5(bottom[7]),
    .in_6(in_4[6]), .in_7(above[7]), .in_8(bottom[6]), .in_9(above[6]), .in_10(above[5]),
    .born(cell_6_born_2), .out_13(cell_7_out_13), .out_14(cell_7_out_14), .born_2(cell_7_born_2),
    .surv_2(cell_7_surv_2), .out_15(out_6[6]));
  \cell  cell_8 (
    .surv(cell_7_surv_2), .in_2(cell_7_out_14), .in_3(cell_9_out_13), .in_4(bottom[6]), .in_5(bottom[8]),
    .in_6(in_4[7]), .in_7(above[8]), .in_8(bottom[7]), .in_9(above[7]), .in_10(above[6]),
    .born(cell_7_born_2), .out_13(cell_8_out_13), .out_14(cell_8_out_14), .born_2(cell_8_born_2),
    .surv_2(cell_8_surv_2), .out_15(out_6[7]));
  \cell  cell_9 (
    .surv(cell_8_surv_2), .in_2(cell_8_out_14), .in_3(cell_10_out_13), .in_4(bottom[7]), .in_5(bottom[9]),
    .in_6(in_4[8]), .in_7(above[9]), .in_8(bottom[8]), .in_9(above[8]), .in_10(above[7]),
    .born(cell_8_born_2), .out_13(cell_9_out_13), .out_14(cell_9_out_14), .born_2(cell_9_born_2),
    .surv_2(cell_9_surv_2), .out_15(out_6[8]));
  \cell  cell_10 (
    .surv(cell_9_surv_2), .in_2(cell_9_out_14), .in_3(cell_11_out_13), .in_4(bottom[8]), .in_5(bottom[10]),
    .in_6(in_4[9]), .in_7(above[10]), .in_8(bottom[9]), .in_9(above[9]), .in_10(above[8]),
    .born(cell_9_born_2), .out_13(cell_10_out_13), .out_14(cell_10_out_14), .born_2(cell_10_born_2),
    .surv_2(cell_10_surv_2), .out_15(out_6[9]));
  \cell  cell_11 (
    .surv(cell_10_surv_2), .in_2(cell_10_out_14), .in_3(cell_12_out_13), .in_4(bottom[9]), .in_5(bottom[11]),
    .in_6(in_4[10]), .in_7(above[11]), .in_8(bottom[10]), .in_9(above[10]), .in_10(above[9]),
    .born(cell_10_born_2), .out_13(cell_11_out_13), .out_14(cell_11_out_14), .born_2(cell_11_born_2),
    .surv_2(cell_11_surv_2), .out_15(out_6[10]));
  \cell  cell_12 (
    .surv(cell_11_surv_2), .in_2(cell_11_out_14), .in_3(cell_13_out_13), .in_4(bottom[10]),
    .in_5(bottom[12]), .in_6(in_4[11]), .in_7(above[12]), .in_8(bottom[11]), .in_9(above[11]),
    .in_10(above[10]), .born(cell_11_born_2), .out_13(cell_12_out_13), .out_14(cell_12_out_14),
    .born_2(cell_12_born_2), .surv_2(cell_12_surv_2), .out_15(out_6[11]));
  \cell  cell_13 (
    .surv(cell_12_surv_2), .in_2(cell_12_out_14), .in_3(cell_14_out_13), .in_4(bottom[11]),
    .in_5(bottom[13]), .in_6(in_4[12]), .in_7(above[13]), .in_8(bottom[12]), .in_9(above[12]),
    .in_10(above[11]), .born(cell_12_born_2), .out_13(cell_13_out_13), .out_14(cell_13_out_14),
    .born_2(cell_13_born_2), .surv_2(cell_13_surv_2), .out_15(out_6[12]));
  \cell  cell_14 (
    .surv(cell_13_surv_2), .in_2(cell_13_out_14), .in_3(cell_15_out_13), .in_4(bottom[12]),
    .in_5(bottom[14]), .in_6(in_4[13]), .in_7(above[14]), .in_8(bottom[13]), .in_9(above[13]),
    .in_10(above[12]), .born(cell_13_born_2), .out_13(cell_14_out_13), .out_14(cell_14_out_14),
    .born_2(cell_14_born_2), .surv_2(cell_14_surv_2), .out_15(out_6[13]));
  \cell  cell_15 (
    .surv(cell_14_surv_2), .in_2(cell_14_out_14), .in_3(cell_16_out_13), .in_4(bottom[13]),
    .in_5(bottom[15]), .in_6(in_4[14]), .in_7(above[15]), .in_8(bottom[14]), .in_9(above[14]),
    .in_10(above[13]), .born(cell_14_born_2), .out_13(cell_15_out_13), .out_14(cell_15_out_14),
    .born_2(cell_15_born_2), .surv_2(cell_15_surv_2), .out_15(out_6[14]));
  \cell  cell_16 (
    .surv(cell_15_surv_2), .in_2(cell_15_out_14), .in_3(cell_17_out_13), .in_4(bottom[14]),
    .in_5(bottom[16]), .in_6(in_4[15]), .in_7(above[16]), .in_8(bottom[15]), .in_9(above[15]),
    .in_10(above[14]), .born(cell_15_born_2), .out_13(cell_16_out_13), .out_14(cell_16_out_14),
    .born_2(cell_16_born_2), .surv_2(cell_16_surv_2), .out_15(out_6[15]));
  \cell  cell_17 (
    .surv(cell_16_surv_2), .in_2(cell_16_out_14), .in_3(cell_18_out_13), .in_4(bottom[15]),
    .in_5(bottom[17]), .in_6(in_4[16]), .in_7(above[17]), .in_8(bottom[16]), .in_9(above[16]),
    .in_10(above[15]), .born(cell_16_born_2), .out_13(cell_17_out_13), .out_14(cell_17_out_14),
    .born_2(cell_17_born_2), .surv_2(cell_17_surv_2), .out_15(out_6[16]));
  \cell  cell_18 (
    .surv(cell_17_surv_2), .in_2(cell_17_out_14), .in_3(cell_19_out_13), .in_4(bottom[16]),
    .in_5(bottom[18]), .in_6(in_4[17]), .in_7(above[18]), .in_8(bottom[17]), .in_9(above[17]),
    .in_10(above[16]), .born(cell_17_born_2), .out_13(cell_18_out_13), .out_14(cell_18_out_14),
    .born_2(cell_18_born_2), .surv_2(cell_18_surv_2), .out_15(out_6[17]));
  \cell  cell_19 (
    .surv(cell_18_surv_2), .in_2(cell_18_out_14), .in_3(cell_20_out_13), .in_4(bottom[17]),
    .in_5(bottom[19]), .in_6(in_4[18]), .in_7(above[19]), .in_8(bottom[18]), .in_9(above[18]),
    .in_10(above[17]), .born(cell_18_born_2), .out_13(cell_19_out_13), .out_14(cell_19_out_14),
    .born_2(cell_19_born_2), .surv_2(cell_19_surv_2), .out_15(out_6[18]));
  \cell  cell_20 (
    .surv(cell_19_surv_2), .in_2(cell_19_out_14), .in_3(cell_21_out_13), .in_4(bottom[18]),
    .in_5(bottom[20]), .in_6(in_4[19]), .in_7(above[20]), .in_8(bottom[19]), .in_9(above[19]),
    .in_10(above[18]), .born(cell_19_born_2), .out_13(cell_20_out_13), .out_14(cell_20_out_14),
    .born_2(cell_20_born_2), .surv_2(cell_20_surv_2), .out_15(out_6[19]));
  \cell  cell_21 (
    .surv(cell_20_surv_2), .in_2(cell_20_out_14), .in_3(cell_22_out_13), .in_4(bottom[19]),
    .in_5(bottom[21]), .in_6(in_4[20]), .in_7(above[21]), .in_8(bottom[20]), .in_9(above[20]),
    .in_10(above[19]), .born(cell_20_born_2), .out_13(cell_21_out_13), .out_14(cell_21_out_14),
    .born_2(cell_21_born_2), .surv_2(cell_21_surv_2), .out_15(out_6[20]));
  \cell  cell_22 (
    .surv(cell_21_surv_2), .in_2(cell_21_out_14), .in_3(cell_23_out_13), .in_4(bottom[20]),
    .in_5(bottom[22]), .in_6(in_4[21]), .in_7(above[22]), .in_8(bottom[21]), .in_9(above[21]),
    .in_10(above[20]), .born(cell_21_born_2), .out_13(cell_22_out_13), .out_14(cell_22_out_14),
    .born_2(cell_22_born_2), .surv_2(cell_22_surv_2), .out_15(out_6[21]));
  \cell  cell_23 (
    .surv(cell_22_surv_2), .in_2(cell_22_out_14), .in_3(cell_24_out_13), .in_4(bottom[21]),
    .in_5(bottom[23]), .in_6(in_4[22]), .in_7(above[23]), .in_8(bottom[22]), .in_9(above[22]),
    .in_10(above[21]), .born(cell_22_born_2), .out_13(cell_23_out_13), .out_14(cell_23_out_14),
    .born_2(cell_23_born_2), .surv_2(cell_23_surv_2), .out_15(out_6[22]));
  \cell  cell_24 (
    .surv(cell_23_surv_2), .in_2(cell_23_out_14), .in_3(cell_25_out_13), .in_4(bottom[22]),
    .in_5(bottom[24]), .in_6(in_4[23]), .in_7(above[24]), .in_8(bottom[23]), .in_9(above[23]),
    .in_10(above[22]), .born(cell_23_born_2), .out_13(cell_24_out_13), .out_14(cell_24_out_14),
    .born_2(cell_24_born_2), .surv_2(cell_24_surv_2), .out_15(out_6[23]));
  \cell  cell_25 (
    .surv(cell_24_surv_2), .in_2(cell_24_out_14), .in_3(cell_26_out_13), .in_4(bottom[23]),
    .in_5(bottom[25]), .in_6(in_4[24]), .in_7(above[25]), .in_8(bottom[24]), .in_9(above[24]),
    .in_10(above[23]), .born(cell_24_born_2), .out_13(cell_25_out_13), .out_14(cell_25_out_14),
    .born_2(cell_25_born_2), .surv_2(cell_25_surv_2), .out_15(out_6[24]));
  \cell  cell_26 (
    .surv(cell_25_surv_2), .in_2(cell_25_out_14), .in_3(cell_27_out_13), .in_4(bottom[24]),
    .in_5(bottom[26]), .in_6(in_4[25]), .in_7(above[26]), .in_8(bottom[25]), .in_9(above[25]),
    .in_10(above[24]), .born(cell_25_born_2), .out_13(cell_26_out_13), .out_14(cell_26_out_14),
    .born_2(cell_26_born_2), .surv_2(cell_26_surv_2), .out_15(out_6[25]));
  \cell  cell_27 (
    .surv(cell_26_surv_2), .in_2(cell_26_out_14), .in_3(cell_28_out_13), .in_4(bottom[25]),
    .in_5(bottom[27]), .in_6(in_4[26]), .in_7(above[27]), .in_8(bottom[26]), .in_9(above[26]),
    .in_10(above[25]), .born(cell_26_born_2), .out_13(cell_27_out_13), .out_14(cell_27_out_14),
    .born_2(cell_27_born_2), .surv_2(cell_27_surv_2), .out_15(out_6[26]));
  \cell  cell_28 (
    .surv(cell_27_surv_2), .in_2(cell_27_out_14), .in_3(cell_29_out_13), .in_4(bottom[26]),
    .in_5(bottom[28]), .in_6(in_4[27]), .in_7(above[28]), .in_8(bottom[27]), .in_9(above[27]),
    .in_10(above[26]), .born(cell_27_born_2), .out_13(cell_28_out_13), .out_14(cell_28_out_14),
    .born_2(cell_28_born_2), .surv_2(cell_28_surv_2), .out_15(out_6[27]));
  \cell  cell_29 (
    .surv(cell_28_surv_2), .in_2(cell_28_out_14), .in_3(cell_30_out_13), .in_4(bottom[27]),
    .in_5(bottom[29]), .in_6(in_4[28]), .in_7(above[29]), .in_8(bottom[28]), .in_9(above[28]),
    .in_10(above[27]), .born(cell_28_born_2), .out_13(cell_29_out_13), .out_14(cell_29_out_14),
    .born_2(cell_29_born_2), .surv_2(cell_29_surv_2), .out_15(out_6[28]));
  \cell  cell_30 (
    .surv(cell_29_surv_2), .in_2(cell_29_out_14), .in_3(cell_31_out_13), .in_4(bottom[28]),
    .in_5(bottom[30]), .in_6(in_4[29]), .in_7(above[30]), .in_8(bottom[29]), .in_9(above[29]),
    .in_10(above[28]), .born(cell_29_born_2), .out_13(cell_30_out_13), .out_14(cell_30_out_14),
    .born_2(cell_30_born_2), .surv_2(cell_30_surv_2), .out_15(out_6[29]));
  \cell  cell_31 (
    .surv(cell_30_surv_2), .in_2(cell_30_out_14), .in_3(cell_32_out_13), .in_4(bottom[29]),
    .in_5(bottom[31]), .in_6(in_4[30]), .in_7(above[31]), .in_8(bottom[30]), .in_9(above[30]),
    .in_10(above[29]), .born(cell_30_born_2), .out_13(cell_31_out_13), .out_14(cell_31_out_14),
    .born_2(cell_31_born_2), .surv_2(cell_31_surv_2), .out_15(out_6[30]));
  \cell  cell_32 (
    .surv(cell_31_surv_2), .in_2(cell_31_out_14), .in_3(1'b0), .in_4(bottom[30]), .in_5(1'b0),
    .in_6(in_4[31]), .in_7(1'b0), .in_8(bottom[31]), .in_9(above[31]), .in_10(above[30]),
    .born(cell_31_born_2), .out_13(cell_32_out_13), .out_15(out_6[31]));  // open: out_14, born_2, surv_2
endmodule

module \cell  (
  input  [8:0] surv,
  input  in_2,
  input  in_3,
  input  in_4,
  input  in_5,
  input  in_6,
  input  in_7,
  input  in_8,
  input  in_9,
  input  in_10,
  input  [8:0] born,
  output [8:0] surv_2,
  output out_13,
  output out_14,
  output out_15,
  output [8:0] born_2
);

  wire multiplexer_1_out, multiplexer_2_out, or_1_out, or_2_out, or_3_out;
  wire [3:0] counter_1_out_9;

  counter counter_1 (
    .in_1(in_2), .in_2(in_3), .in_3(in_4), .in_4(in_5), .in_5(in_7), .in_6(in_8), .in_7(in_9), .in_8(in_10),
    .out_9(counter_1_out_9));
  Multiplexer #(.select(4), .enable("false")) multiplexer_1 (
    .in0(surv[0]), .in1(surv[1]), .in2(surv[2]), .in3(surv[3]), .in4(surv[4]), .in5(surv[5]), .in6(surv[6]),
    .in7(surv[7]), .in8(surv[8]), .out(multiplexer_1_out), .sel(counter_1_out_9));  // open: in9, in10, in11, in12, in13, in14, in15
  Multiplexer #(.select(4), .enable("false")) multiplexer_2 (
    .in0(born[0]), .in1(born[1]), .in2(born[2]), .in3(born[3]), .in4(born[4]), .in5(born[5]), .in6(born[6]),
    .in7(born[7]), .in8(born[8]), .out(multiplexer_2_out), .sel(counter_1_out_9));  // open: in9, in10, in11, in12, in13, in14, in15
  or or_1 (or_1_out, multiplexer_1_out, multiplexer_2_out, in_6);
  or or_2 (or_2_out, multiplexer_1_out, multiplexer_2_out, ~in_6);  // OR_Gate
  or or_3 (or_3_out, ~multiplexer_1_out, multiplexer_2_out, in_6);  // OR_Gate
  and and_1 (out_15, or_1_out, or_2_out, or_3_out);

  assign born_2 = born;
  assign out_13 = in_6;
  assign out_14 = in_6;
  assign surv_2 = surv;
endmodule

module counter (
  input  in_1,
  input  in_2,
  input  in_3,
  input  in_4,
  input  in_5,
  input  in_6,
  input  in_7,
  input  in_8,
  output [3:0] out_9
);

  wire [1:0] adder_1_out, adder_2_out, adder_3_out, adder_4_out, adder_5_out, adder_6_out;
  wire [2:2] adder_5_cout, adder_6_cout;

  Adder #(.width(1)) adder_1 (.a(in_1), .b(in_2), .out(adder_1_out[0]), .cout(adder_1_out[1]));  // open: cin
  Adder #(.width(1)) adder_2 (.a(in_3), .b(in_4), .out(adder_2_out[0]), .cout(adder_2_out[1]));  // open: cin
  Adder #(.width(1)) adder_3 (.a(in_5), .b(in_6), .out(adder_3_out[0]), .cout(adder_3_out[1]));  // open: cin
  Adder #(.width(1)) adder_4 (.a(in_7), .b(in_8), .out(adder_4_out[0]), .cout(adder_4_out[1]));  // open: cin
  Adder #(.width(2)) adder_5 (
    .a(adder_1_out), .b(adder_2_out), .out(adder_5_out), .cout(adder_5_cout[2]));  // open: cin
  Adder #(.width(2)) adder_6 (
    .a(adder_3_out), .b(adder_4_out), .out(adder_6_out), .cout(adder_6_cout[2]));  // open: cin
  Adder #(.width(3)) adder_7 (
    .a({adder_5_cout[2], adder_5_out}), .b({adder_6_cout[2], adder_6_out}), .out(out_9[2:0]), .cout(out_9[3]));  // open: cin
endmodule

module gameProcessor (
  input  clock,
  input  play,
  input  [8:0] surv,
  input  [8:0] born,
  input  [31:0] in_5,
  input  [31:0] in_6,
  input  [31:0] in_7,
  input  [31:0] in_8,
  input  [31:0] in_9,
  input  [31:0] in_10,
  input  [31:0] in_11,
  input  [31:0] in_12,
  input  [31:0] in_13,
  input  [31:0] in_14,
  input  [31:0] in_15,
  input  [31:0] in_16,
  input  [31:0] in_17,
  input  [31:0] in_18,
  input  [31:0] in_19,
  input  [31:0] in_20,
  input  [31:0] in_21,
  input  [31:0] in_22,
  input  [31:0] in_23,
  input  [31:0] in_24,
  input  [31:0] in_25,
  input  [31:0] in_26,
  input  [31:0] in_27,
  input  [31:0] in_28,
  input  [31:0] in_29,
  input  [31:0] in_30,
  input  [31:0] in_31,
  input  [31:0] in_32,
  input  [31:0] in_33,
  input  [31:0] in_34,
  input  [31:0] in_35,
  input  [31:0] in_36,
  output cc,
  output [31:0] out_38,
  output [31:0] out_39,
  output [31:0] out_40,
  output [31:0] out_41,
  output [31:0] out_42,
  output [31:0] out_43,
  output [31:0] out_44,
  output [31:0] out_45,
  output [31:0] out_46,
  output [31:0] out_47,
  output [31:0] out_48,
  output [31:0] out_49,
  output [31:0] out_50,
  output [31:0] out_51,
  output [31:0] out_52,
  output [31:0] out_53,
  output [31:0] out_54,
  output [31:0] out_55,
  output [31:0] out_56,
  output [31:0] out_57,
  output [31:0] out_58,
  output [31:0] out_59,
  output [31:0] out_60,
  output [31:0] out_61,
  output [31:0] out_62,
  output [31:0] out_63,
  output [31:0] out_64,
  output [31:0] out_65,
  output [31:0] out_66,
  output [31:0] out_67,
  output [31:0] out_68,
  output [31:0] out_69
);

  wire comparator_1_eq, nor_1_out, not_1_out, not_2_out;
  wire [4:0] cnt;
  wire [31:0] demultiplexer_1_out0, gameprocessorrow_1_out_6, multiplexer_1_out, multiplexer_2_out,
       multiplexer_3_out;

  not not_1 (not_1_out, comparator_1_eq);
  and and_1 (cc, not_1_out, comparator_1_eq);
  Comparator #(.width(5)) comparator_1 (.a({5{1'b0}}), .b(cnt), .eq(comparator_1_eq));  // open: gt, lt
  Counter #(.width(5), .max('h1f), .trigger("falling")) counter_1 (
    .count(play), .Q(cnt), .clk(clock), .clr(nor_1_out));  // open: load, D, carry
  nor nor_1 (nor_1_out, play, not_2_out);
  not not_2 (not_2_out, play);
  Multiplexer #(.select(5), .width(32)) multiplexer_1 (
    .in0({32{1'b0}}), .in1(in_5), .in2(in_6), .in3(in_7), .in4(in_8), .in5(in_9), .in6(in_10), .in7(in_11),
    .in8(in_12), .in9(in_13), .in10(in_14), .in11(in_15), .in12(in_16), .in13(in_17), .in14(in_18),
    .in15(in_19), .in16(in_20), .in17(in_21), .in18(in_22), .in19(in_23), .in20(in_24), .in21(in_25),
    .in22(in_26), .in23(in_27), .in24(in_28), .in25(in_29), .in26(in_30), .in27(in_31), .in28(in_32),
    .in29(in_33), .in30(in_34), .in31(in_35), .out(multiplexer_1_out), .sel(cnt), .en(play));
  Multiplexer #(.select(5), .width(32)) multiplexer_2 (
    .in0(in_5), .in1(in_6), .in2(in_7), .in3(in_8), .in4(in_9), .in5(in_10), .in6(in_11), .in7(in_12),
    .in8(in_13), .in9(in_14), .in10(in_15), .in11(in_16), .in12(in_17), .in13(in_18), .in14(in_19),
    .in15(in_20), .in16(in_21), .in17(in_22), .in18(in_23), .in19(in_24), .in20(in_25), .in21(in_26),
    .in22(in_27), .in23(in_28), .in24(in_29), .in25(in_30), .in26(in_31), .in27(in_32), .in28(in_33),
    .in29(in_34), .in30(in_35), .in31(in_36), .out(multiplexer_2_out), .sel(cnt), .en(play));
  Multiplexer #(.select(5), .width(32)) multiplexer_3 (
    .in0(in_6), .in1(in_7), .in2(in_8), .in3(in_9), .in4(in_10), .in5(in_11), .in6(in_12), .in7(in_13),
    .in8(in_14), .in9(in_15), .in10(in_16), .in11(in_17), .in12(in_18), .in13(in_19), .in14(in_20),
    .in15(in_21), .in16(in_22), .in17(in_23), .in18(in_24), .in19(in_25), .in20(in_26), .in21(in_27),
    .in22(in_28), .in23(in_29), .in24(in_30), .in25(in_31), .in26(in_32), .in27(in_33), .in28(in_34),
    .in29(in_35), .in30(in_36), .in31({32{1'b0}}), .out(multiplexer_3_out), .sel(cnt), .en(play));
  gameProcessorrow gameprocessorrow_1 (
    .in_4(multiplexer_2_out), .out_6(gameprocessorrow_1_out_6), .surv(surv), .born(born),
    .bottom(multiplexer_1_out), .above(multiplexer_3_out));
  Demultiplexer #(.select(5), .disabled(0)) demultiplexer_1 (
    .out0(demultiplexer_1_out0[0]), .out1(demultiplexer_1_out0[1]), .out2(demultiplexer_1_out0[2]),
    .out3(demultiplexer_1_out0[3]), .out4(demultiplexer_1_out0[4]), .out5(demultiplexer_1_out0[5]),
    .out6(demultiplexer_1_out0[6]), .out7(demultiplexer_1_out0[7]), .out8(demultiplexer_1_out0[8]),
    .out9(demultiplexer_1_out0[9]), .out10(demultiplexer_1_out0[10]), .out11(demultiplexer_1_out0[11]),
    .out12(demultiplexer_1_out0[12]), .out13(demultiplexer_1_out0[13]), .out14(demultiplexer_1_out0[14]),
    .out15(demultiplexer_1_out0[15]), .out16(demultiplexer_1_out0[16]), .out17(demultiplexer_1_out0[17]),
    .out18(demultiplexer_1_out0[18]), .out19(demultiplexer_1_out0[19]), .out20(demultiplexer_1_out0[20]),
    .out21(demultiplexer_1_out0[21]), .out22(demultiplexer_1_out0[22]), .out23(demultiplexer_1_out0[23]),
    .out24(demultiplexer_1_out0[24]), .out25(demultiplexer_1_out0[25]), .out26(demultiplexer_1_out0[26]),
    .out27(demultiplexer_1_out0[27]), .out28(demultiplexer_1_out0[28]), .out29(demultiplexer_1_out0[29]),
    .out30(demultiplexer_1_out0[30]), .out31(demultiplexer_1_out0[31]), .in(clock), .sel(cnt), .en(play));
  Register #(.width(32)) register_1 (
    .D(gameprocessorrow_1_out_6), .Q(out_38), .clk(demultiplexer_1_out0[0]));  // open: en, clr
  Register #(.width(32)) register_2 (
    .D(gameprocessorrow_1_out_6), .Q(out_39), .clk(demultiplexer_1_out0[1]));  // open: en, clr
  Register #(.width(32)) register_3 (
    .D(gameprocessorrow_1_out_6), .Q(out_40), .clk(demultiplexer_1_out0[2]));  // open: en, clr
  Register #(.width(32)) register_4 (
    .D(gameprocessorrow_1_out_6), .Q(out_41), .clk(demultiplexer_1_out0[3]));  // open: en, clr
  Register #(.width(32)) register_5 (
    .D(gameprocessorrow_1_out_6), .Q(out_42), .clk(demultiplexer_1_out0[4]));  // open: en, clr
  Register #(.width(32)) register_6 (
    .D(gameprocessorrow_1_out_6), .Q(out_43), .clk(demultiplexer_1_out0[5]));  // open: en, clr
  Register #(.width(32)) register_7 (
    .D(gameprocessorrow_1_out_6), .Q(out_44), .clk(demultiplexer_1_out0[6]));  // open: en, clr
  Register #(.width(32)) register_8 (
    .D(gameprocessorrow_1_out_6), .Q(out_45), .clk(demultiplexer_1_out0[7]));  // open: en, clr
  Register #(.width(32)) register_9 (
    .D(gameprocessorrow_1_out_6), .Q(out_46), .clk(demultiplexer_1_out0[8]));  // open: en, clr
  Register #(.width(32)) register_10 (
    .D(gameprocessorrow_1_out_6), .Q(out_47), .clk(demultiplexer_1_out0[9]));  // open: en, clr
  Register #(.width(32)) register_11 (
    .D(gameprocessorrow_1_out_6), .Q(out_48), .clk(demultiplexer_1_out0[10]));  // open: en, clr
  Register #(.width(32)) register_12 (
    .D(gameprocessorrow_1_out_6), .Q(out_49), .clk(demultiplexer_1_out0[11]));  // open: en, clr
  Register #(.width(32)) register_13 (
    .D(gameprocessorrow_1_out_6), .Q(out_50), .clk(demultiplexer_1_out0[12]));  // open: en, clr
  Register #(.width(32)) register_14 (
    .D(gameprocessorrow_1_out_6), .Q(out_51), .clk(demultiplexer_1_out0[13]));  // open: en, clr
  Register #(.width(32)) register_15 (
    .D(gameprocessorrow_1_out_6), .Q(out_52), .clk(demultiplexer_1_out0[14]));  // open: en, clr
  Register #(.width(32)) register_16 (
    .D(gameprocessorrow_1_out_6), .Q(out_53), .clk(demultiplexer_1_out0[15]));  // open: en, clr
  Register #(.width(32)) register_17 (
    .D(gameprocessorrow_1_out_6), .Q(out_54), .clk(demultiplexer_1_out0[16]));  // open: en, clr
  Register #(.width(32)) register_18 (
    .D(gameprocessorrow_1_out_6), .Q(out_55), .clk(demultiplexer_1_out0[17]));  // open: en, clr
  Register #(.width(32)) register_19 (
    .D(gameprocessorrow_1_out_6), .Q(out_56), .clk(demultiplexer_1_out0[18]));  // open: en, clr
  Register #(.width(32)) register_20 (
    .D(gameprocessorrow_1_out_6), .Q(out_57), .clk(demultiplexer_1_out0[19]));  // open: en, clr
  Register #(.width(32)) register_21 (
    .D(gameprocessorrow_1_out_6), .Q(out_58), .clk(demultiplexer_1_out0[20]));  // open: en, clr
  Register #(.width(32)) register_22 (
    .D(gameprocessorrow_1_out_6), .Q(out_59), .clk(demultiplexer_1_out0[21]));  // open: en, clr
  Register #(.width(32)) register_23 (
    .D(gameprocessorrow_1_out_6), .Q(out_60), .clk(demultiplexer_1_out0[22]));  // open: en, clr
  Register #(.width(32)) register_24 (
    .D(gameprocessorrow_1_out_6), .Q(out_61), .clk(demultiplexer_1_out0[23]));  // open: en, clr
  Register #(.width(32)) register_25 (
    .D(gameprocessorrow_1_out_6), .Q(out_62), .clk(demultiplexer_1_out0[24]));  // open: en, clr
  Register #(.width(32)) register_26 (
    .D(gameprocessorrow_1_out_6), .Q(out_63), .clk(demultiplexer_1_out0[25]));  // open: en, clr
  Register #(.width(32)) register_27 (
    .D(gameprocessorrow_1_out_6), .Q(out_64), .clk(demultiplexer_1_out0[26]));  // open: en, clr
  Register #(.width(32)) register_28 (
    .D(gameprocessorrow_1_out_6), .Q(out_65), .clk(demultiplexer_1_out0[27]));  // open: en, clr
  Register #(.width(32)) register_29 (
    .D(gameprocessorrow_1_out_6), .Q(out_66), .clk(demultiplexer_1_out0[28]));  // open: en, clr
  Register #(.width(32)) register_30 (
    .D(gameprocessorrow_1_out_6), .Q(out_67), .clk(demultiplexer_1_out0[29]));  // open: en, clr
  Register #(.width(32)) register_31 (
    .D(gameprocessorrow_1_out_6), .Q(out_68), .clk(demultiplexer_1_out0[30]));  // open: en, clr
  Register #(.width(32)) register_32 (
    .D(gameprocessorrow_1_out_6), .Q(out_69), .clk(demultiplexer_1_out0[31]));  // open: en, clr

  // Other names for the same wires on the sheet: wi0[31:0] = out_38; wi1[31:0] = out_39; wi2[31:0] = out_40;
  //   wi3[31:0] = out_41; wi4[31:0] = out_42; wi5[31:0] = out_43; wi6[31:0] = out_44; wi7[31:0] = out_45;
  //   wi8[31:0] = out_46; wi9[31:0] = out_47; wi10[31:0] = out_48; wi11[31:0] = out_49; wi12[31:0] = out_50;
  //   wi13[31:0] = out_51; wi14[31:0] = out_52; wi15[31:0] = out_53; wi16[31:0] = out_54; wi17[31:0] = out_55;
  //   wi18[31:0] = out_56; wi19[31:0] = out_57; wi20[31:0] = out_58; wi21[31:0] = out_59; wi22[31:0] = out_60;
  //   wi23[31:0] = out_61; wi24[31:0] = out_62; wi25[31:0] = out_63; wi26[31:0] = out_64; wi27[31:0] = out_65;
  //   wi28[31:0] = out_66; wi29[31:0] = out_67; wi30[31:0] = out_68; wi31[31:0] = out_69; wo0[31:0] = in_5;
  //   wo1[31:0] = in_6; wo2[31:0] = in_7; wo3[31:0] = in_8; wo4[31:0] = in_9; wo5[31:0] = in_10; wo6[31:0] = in_11;
  //   wo7[31:0] = in_12; wo8[31:0] = in_13; wo9[31:0] = in_14; wo10[31:0] = in_15; wo11[31:0] = in_16;
  //   wo12[31:0] = in_17; wo13[31:0] = in_18; wo14[31:0] = in_19; wo15[31:0] = in_20; wo16[31:0] = in_21;
  //   wo17[31:0] = in_22; wo18[31:0] = in_23; wo19[31:0] = in_24; wo20[31:0] = in_25; wo21[31:0] = in_26;
  //   wo22[31:0] = in_27; wo23[31:0] = in_28; wo24[31:0] = in_29; wo25[31:0] = in_30; wo26[31:0] = in_31;
  //   wo27[31:0] = in_32; wo28[31:0] = in_33; wo29[31:0] = in_34; wo30[31:0] = in_35; wo31[31:0] = in_36
endmodule
