// Logisim project matrixIO.circ as structural Verilog: 1 circuit, main circuit main
module main (
  input  in_out_prime,
  input  [7:0] I_Oaddr,
  input  I_Osel,
  input  [15:0] I_Odat,
  input  reset,
  input  clock,
  output [15:0] I_Odat_2,
  output [31:0] out_8,
  output [31:0] out_9,
  output [31:0] out_10,
  output [31:0] out_11,
  output [31:0] out_12,
  output [31:0] out_13,
  output [31:0] out_14,
  output [31:0] out_15,
  output [31:0] out_16,
  output [31:0] out_17,
  output [31:0] out_18,
  output [31:0] out_19,
  output [31:0] out_20,
  output [31:0] out_21,
  output [31:0] out_22,
  output [31:0] out_23,
  output [31:0] out_24,
  output [31:0] out_25,
  output [31:0] out_26,
  output [31:0] out_27,
  output [31:0] out_28,
  output [31:0] out_29,
  output [31:0] out_30,
  output [31:0] out_31,
  output [31:0] out_32,
  output [31:0] out_33,
  output [31:0] out_34,
  output [31:0] out_35,
  output [31:0] out_36,
  output [31:0] out_37,
  output [31:0] out_38,
  output [31:0] out_39
);

  wire and_1_out, and_2_out, and_3_out, and_4_out, and_5_out, and_6_out, controlled_buffer_3_out,
       controlled_buffer_9_out, not_1_out, or_1_out, or_2_out;
  wire [3:0] controlled_buffer_7_out, controlled_buffer_10_out, controlled_buffer_11_out;
  wire [5:0] controlled_buffer_4_out;
  wire [15:0] controlled_buffer_1_out, controlled_buffer_6_out, controlled_buffer_8_out, main_1_dataout,
       status_q;

  and and_1 (and_1_out, ~I_Oaddr[7], I_Oaddr[6], I_Oaddr[5], I_Oaddr[4], I_Oaddr[3], I_Oaddr[2], I_Oaddr[1], ~I_Oaddr[0]);  // AND_Gate
  and and_2 (and_2_out, I_Osel, and_1_out);
  assign controlled_buffer_1_out = and_3_out ? I_Odat : 16'bz;  // Controlled_Buffer controlled_buffer_1
  and and_3 (and_3_out, ~in_out_prime, and_2_out);  // AND_Gate
  assign I_Odat_2 = and_4_out ? status_q : 16'bz;  // Controlled_Buffer controlled_buffer_2
  and and_4 (and_4_out, in_out_prime, and_2_out);
  Register #(.width(16)) status (.D(controlled_buffer_1_out), .en(and_2_out), .Q(status_q), .clk(clock), .clr(reset));
  and and_5 (and_5_out, in_out_prime, and_2_out, I_Odat[13]);
  and and_6 (and_6_out, I_Osel, I_Oaddr[7]);
  assign controlled_buffer_3_out = and_6_out ? in_out_prime : 1'bz;  // Controlled_Buffer controlled_buffer_3
  assign controlled_buffer_4_out = and_6_out ? I_Oaddr[6:1] : 6'bz;  // Controlled_Buffer controlled_buffer_4
  assign I_Odat_2 = in_out_prime ? main_1_dataout : 16'bz;  // Controlled_Buffer controlled_buffer_5
  not not_1 (not_1_out, in_out_prime);
  assign controlled_buffer_6_out = not_1_out ? I_Odat : 16'bz;  // Controlled_Buffer controlled_buffer_6
  assign controlled_buffer_7_out = status_q[12] ? status_q[3:0] : 4'bz;  // Controlled_Buffer controlled_buffer_7
  assign controlled_buffer_8_out = and_6_out ? controlled_buffer_6_out : 16'bz;  // Controlled_Buffer controlled_buffer_8
  or or_1 (or_1_out, status_q[12], and_6_out);
  assign controlled_buffer_9_out = or_1_out ? clock : 1'bz;  // Controlled_Buffer controlled_buffer_9
  Matrix_Controller_main main_1 (
    .sel(and_6_out), .play(status_q[12]), .reset(or_2_out), .out_12(out_8), .out_13(out_9), .out_14(out_10),
    .out_15(out_11), .out_16(out_12), .out_17(out_13), .out_18(out_14), .out_19(out_15), .out_20(out_16),
    .out_21(out_17), .out_22(out_18), .out_23(out_19), .out_24(out_20), .out_25(out_21), .out_26(out_22),
    .out_27(out_23), .out_28(out_24), .clock(controlled_buffer_9_out), .out_29(out_25), .out_30(out_26),
    .out_31(out_27), .out_32(out_28), .out_33(out_29), .out_34(out_30), .out_35(out_31), .out_42(out_38),
    .out_43(out_39), .addr(controlled_buffer_4_out), .die1(controlled_buffer_7_out),
    .die2(controlled_buffer_10_out), .respawn(controlled_buffer_11_out), .out_36(out_32), .out_37(out_33),
    .out_38(out_34), .out_39(out_35), .out_40(out_36), .out_41(out_37), .datain(controlled_buffer_8_out),
    .dataout(main_1_dataout), .rd_wr_prime(controlled_buffer_3_out));
  assign controlled_buffer_10_out = status_q[12] ? status_q[7:4] : 4'bz;  // Controlled_Buffer controlled_buffer_10
  assign controlled_buffer_11_out = status_q[12] ? status_q[11:8] : 4'bz;  // Controlled_Buffer controlled_buffer_11
  or or_2 (or_2_out, and_5_out, reset);

  // Other names for the same wires on the sheet: o0[31:0] = out_8; o1[31:0] = out_9; o2[31:0] = out_10;
  //   o3[31:0] = out_11; o4[31:0] = out_12; o5[31:0] = out_13; o6[31:0] = out_14; o7[31:0] = out_15;
  //   o8[31:0] = out_16; o9[31:0] = out_17; o10[31:0] = out_18; o11[31:0] = out_19; o12[31:0] = out_20;
  //   o13[31:0] = out_21; o14[31:0] = out_22; o15[31:0] = out_23; o16[31:0] = out_24; o17[31:0] = out_25;
  //   o18[31:0] = out_26; o19[31:0] = out_27; o20[31:0] = out_28; o21[31:0] = out_29; o22[31:0] = out_30;
  //   o23[31:0] = out_31; o24[31:0] = out_32; o25[31:0] = out_33; o26[31:0] = out_34; o27[31:0] = out_35;
  //   o28[31:0] = out_36; o29[31:0] = out_37; o30[31:0] = out_38; o31[31:0] = out_39
endmodule
